// Logisim project RegFile.circ as structural Verilog: 3 circuits, main circuit main
module main (
  input  [15:0] WriteData0,
  input  [15:0] WriteData1,
  input  [2:0] WriteSelect0,
  input  [2:0] ReadSelect0,
  input  [2:0] ReadSelect1,
  input  WE0,
  input  WE1,
  input  Clock,
  output [15:0] Reg0,
  output [15:0] Reg1,
  output [15:0] Reg2,
  output [15:0] Reg3,
  output [15:0] Reg4,
  output [15:0] Reg5,
  output [15:0] Reg6,
  output [15:0] Reg7,
  output [15:0] ReadData0,
  output [15:0] ReadData1
);

  wire decoder_1_out0, decoder_1_out1, decoder_1_out2, decoder_1_out3, decoder_1_out4, decoder_1_out5,
       decoder_1_out6, decoder_1_out7, decoder_2_out0, decoder_2_out2, decoder_2_out3, decoder_2_out4,
       decoder_2_out5, decoder_2_out6, decoder_2_out7, or_1_p2, or_1_p3, or_2_out, or_3_out, or_4_out,
       or_5_out, or_6_out, or_7_out, or_8_out, undriven, undriven_2, undriven_3, undriven_4;
  wire [2:0] WriteSelect1;
  wire [15:0] adder_2_out, adder_3_out, adder_4_out, adder_5_out, adder_6_out, adder_7_out, adder_8_out,
       adder_9_out, demultiplexer_1_out0, demultiplexer_1_out1, demultiplexer_1_out2, demultiplexer_1_out3,
       demultiplexer_1_out4, demultiplexer_1_out5, demultiplexer_1_out6, demultiplexer_1_out7,
       demultiplexer_2_p1, demultiplexer_2_p3, demultiplexer_2_p4, demultiplexer_2_p5, demultiplexer_2_p6,
       demultiplexer_2_p8, demultiplexer_2_p9, demultiplexer_2_p10;

  Demultiplexer #(.select(3), .width(16), .disabled(0)) demultiplexer_1 (
    .out0(demultiplexer_1_out0), .out1(demultiplexer_1_out1), .out2(demultiplexer_1_out2),
    .out3(demultiplexer_1_out3), .out4(demultiplexer_1_out4), .out5(demultiplexer_1_out5),
    .out6(demultiplexer_1_out6), .out7(demultiplexer_1_out7), .in(WriteData0), .sel(WriteSelect0));  // open: en
  Adder #(.width(3)) adder_1 (.a(WriteSelect0), .b(3'b001), .out(WriteSelect1));  // open: cin, cout
  // Demultiplexer #(.select(3), .width(16), .disabled(0)) demultiplexer_2: pin names not known; wires that end beside it: demultiplexer_2_p1, WriteSelect1, demultiplexer_2_p3, demultiplexer_2_p4, demultiplexer_2_p5, demultiplexer_2_p6, WriteData1, demultiplexer_2_p8, demultiplexer_2_p9, demultiplexer_2_p10
  Adder #(.width(16)) adder_2 (.a(demultiplexer_1_out0), .b(demultiplexer_2_p1), .out(adder_2_out));  // open: cin, cout
  Adder #(.width(16)) adder_3 (.a(demultiplexer_1_out1), .b(demultiplexer_2_p3), .out(adder_3_out));  // open: cin, cout
  Adder #(.width(16)) adder_4 (.a(demultiplexer_1_out2), .b(demultiplexer_2_p4), .out(adder_4_out));  // open: cin, cout
  Adder #(.width(16)) adder_5 (.a(demultiplexer_1_out3), .b(demultiplexer_2_p5), .out(adder_5_out));  // open: cin, cout
  Adder #(.width(16)) adder_6 (.a(demultiplexer_1_out4), .b(demultiplexer_2_p6), .out(adder_6_out));  // open: cin, cout
  Adder #(.width(16)) adder_7 (.a(demultiplexer_1_out5), .b(demultiplexer_2_p8), .out(adder_7_out));  // open: cin, cout
  Adder #(.width(16)) adder_8 (.a(demultiplexer_1_out6), .b(demultiplexer_2_p9), .out(adder_8_out));  // open: cin, cout
  Adder #(.width(16)) adder_9 (
    .a(demultiplexer_1_out7), .b(demultiplexer_2_p10), .out(adder_9_out));  // open: cin, cout
  Decoder #(.select(3), .disabled(0), .enable("true")) decoder_1 (
    .out0(decoder_1_out0), .out1(decoder_1_out1), .out2(decoder_1_out2), .out3(decoder_1_out3),
    .out4(decoder_1_out4), .out5(decoder_1_out5), .out6(decoder_1_out6), .out7(decoder_1_out7),
    .sel(WriteSelect0), .en(WE0));
  // OR_Gate or_1: pin names not known; wires that end beside it: decoder_1_out1, or_1_p2, or_1_p3
  or or_2 (or_2_out, decoder_1_out0, decoder_2_out0);
  or or_3 (or_3_out, decoder_1_out2, decoder_2_out2, undriven);
  or or_4 (or_4_out, undriven, decoder_1_out3, decoder_2_out3, undriven_2);
  Register #(.width(16)) register_1 (.D(adder_2_out), .en(or_2_out), .Q(Reg0), .clk(Clock));  // open: clr
  Register #(.width(16)) register_2 (.D(adder_3_out), .en(or_1_p2), .Q(Reg1), .clk(Clock));  // open: clr
  Register #(.width(16)) register_3 (.D(adder_4_out), .en(or_3_out), .Q(Reg2), .clk(Clock));  // open: clr
  Register #(.width(16)) register_4 (.D(adder_5_out), .en(or_4_out), .Q(Reg3), .clk(Clock));  // open: clr
  Register #(.width(16)) register_5 (.D(adder_6_out), .en(or_6_out), .Q(Reg4), .clk(Clock));  // open: clr
  Register #(.width(16)) register_6 (.D(adder_7_out), .en(or_5_out), .Q(Reg5), .clk(Clock));  // open: clr
  Register #(.width(16)) register_7 (.D(adder_8_out), .en(or_7_out), .Q(Reg6), .clk(Clock));  // open: clr
  Register #(.width(16)) register_8 (.D(adder_9_out), .en(or_8_out), .Q(Reg7), .clk(Clock));  // open: clr
  or or_5 (or_5_out, undriven_3, decoder_1_out5, decoder_2_out5, undriven_4);
  or or_6 (or_6_out, undriven_2, decoder_1_out4, decoder_2_out4, undriven_3);
  or or_7 (or_7_out, undriven_4, decoder_1_out6, decoder_2_out6);
  or or_8 (or_8_out, decoder_1_out7, decoder_2_out7);
  Decoder #(.select(3), .disabled(0), .enable("true")) decoder_2 (
    .out0(decoder_2_out0), .out1(or_1_p3), .out2(decoder_2_out2), .out3(decoder_2_out3),
    .out4(decoder_2_out4), .out5(decoder_2_out5), .out6(decoder_2_out6), .out7(decoder_2_out7),
    .sel(WriteSelect1), .en(WE1));
  Multiplexer #(.select(3), .width(16), .disabled(0)) multiplexer_1 (
    .in0(Reg0), .in1(Reg1), .in2(Reg2), .in3(Reg3), .in4(Reg4), .in5(Reg5), .in6(Reg6), .in7(Reg7),
    .out(ReadData0), .sel(ReadSelect0));  // open: en
  Multiplexer #(.select(3), .width(16), .disabled(0)) multiplexer_2 (
    .in0(Reg0), .in1(Reg1), .in2(Reg2), .in3(Reg3), .in4(Reg4), .in5(Reg5), .in6(Reg6), .in7(Reg7),
    .out(ReadData1), .sel(ReadSelect1));  // open: en

  // Other names for the same wires on the sheet: WriteEnable0 = WE0; WriteEnable1 = WE1

  // Notes on the sheet:
  //   Inputs
  //   Add the registers to this file
  //   WriteSelect0 - Register to write to
  //   WE0 - Enable writing to 1 register
  //   ReadSelect0 - First register to read data from
  //   ReadSelect1 - Second register to read data from
  //   WE1 - Enable writing to 2nd register (mul/div)
  //   ReadData0 - Data being read from first register
  //   ReadData1 - Data being read from second register
  //   WriteData0 - The data to be written to register by most instructions
  //   WriteData1 - The data to be written to second register by mul/div
  //   These can be used for debug and testing
  //    Don't modify any of the inputs/outputs in this file!
  //   and design the logic to control them
  //   Outputs
endmodule

module test (
  input  [15:0] Write_data_A,
  input  Write_Enable_Port_A,
  input  [2:0] in_3,
  input  [15:0] Write_data_B,
  input  Write_Enable_Port_B,
  input  [2:0] Select_Read_A,
  input  [2:0] Select_Read_B
);

  wire Clock_out;
  wire [15:0] main_1_readdata0, main_1_readdata1, main_1_reg0, main_1_reg1, main_1_reg2, main_1_reg3,
       main_1_reg4, main_1_reg5, main_1_reg6, main_1_reg7;

  // Probe on main_1_reg0
  // Probe on main_1_reg1
  // Probe on main_1_reg2
  // Probe on main_1_reg3
  Button Clock (.out(Clock_out));
  // Probe on main_1_reg5
  // Probe on main_1_reg4
  // Probe on main_1_reg6
  // Probe on main_1_reg7
  main main_1 (
    .WriteData0(Write_data_A), .WriteData1(Write_data_B), .ReadData0(main_1_readdata0),
    .ReadData1(main_1_readdata1), .WriteSelect0(in_3), .ReadSelect0(Select_Read_A),
    .ReadSelect1(Select_Read_B), .Reg0(main_1_reg0), .Reg1(main_1_reg1), .Reg2(main_1_reg2),
    .Reg3(main_1_reg3), .Reg4(main_1_reg4), .Reg5(main_1_reg5), .Reg6(main_1_reg6), .Reg7(main_1_reg7),
    .WE0(Write_Enable_Port_A), .WE1(Write_Enable_Port_B), .Clock(Clock_out));
  // Probe on main_1_readdata0
  // Probe on main_1_readdata1

  // Notes on the sheet:
  //   Test your circuit!
endmodule

module writeDataSelect (
  input  [15:0] in_1,
  input  [15:0] in_2,
  output [15:0] out_3
);

  // Adder adder_1: pin names not known; wires that end beside it: in_1, in_2, out_3

  // Notes on the sheet:
  //   data0
  //   data1
endmodule
